// Logisim project adder.circ as structural Verilog: 2 circuits, main circuit main
module main (
  input  sub,
  input  [23:0] A,
  input  [23:0] B,
  output [23:0] result,
  output ovf
);

  wire n1_bit_adder_1_carryout, n1_bit_adder_2_carryout, n1_bit_adder_3_carryout, n1_bit_adder_4_carryout,
       n1_bit_adder_5_carryout, n1_bit_adder_6_carryout, n1_bit_adder_7_carryout, n1_bit_adder_8_carryout,
       n1_bit_adder_9_carryout, n1_bit_adder_10_carryout, n1_bit_adder_11_carryout, n1_bit_adder_12_carryout,
       n1_bit_adder_13_carryout, n1_bit_adder_14_carryout, n1_bit_adder_15_carryout,
       n1_bit_adder_16_carryout, n1_bit_adder_17_carryout, n1_bit_adder_18_carryout,
       n1_bit_adder_19_carryout, n1_bit_adder_20_carryout, n1_bit_adder_21_carryout,
       n1_bit_adder_22_carryout, n1_bit_adder_23_carryout, n1_bit_adder_24_carryout, xor_2_out, xor_3_out,
       xor_4_out, xor_5_out, xor_6_out, xor_7_out, xor_8_out, xor_9_out, xor_10_out, xor_11_out, xor_12_out,
       xor_13_out, xor_14_out, xor_15_out, xor_16_out, xor_17_out, xor_18_out, xor_19_out, xor_20_out,
       xor_21_out, xor_22_out, xor_23_out, xor_24_out, xor_25_out;

  xor xor_1 (ovf, n1_bit_adder_1_carryout, n1_bit_adder_2_carryout);
  _1_bit_adder u_1_bit_adder_1 (
    .CarryIn(n1_bit_adder_2_carryout), .a(A[23]), .b(xor_2_out), .Sum(result[23]),
    .CarryOut(n1_bit_adder_1_carryout));
  xor xor_2 (xor_2_out, sub, B[23]);
  _1_bit_adder u_1_bit_adder_2 (
    .CarryIn(n1_bit_adder_3_carryout), .a(A[22]), .b(xor_3_out), .Sum(result[22]),
    .CarryOut(n1_bit_adder_2_carryout));
  xor xor_3 (xor_3_out, sub, B[22]);
  _1_bit_adder u_1_bit_adder_3 (
    .CarryIn(n1_bit_adder_4_carryout), .a(A[21]), .b(xor_4_out), .Sum(result[21]),
    .CarryOut(n1_bit_adder_3_carryout));
  _1_bit_adder u_1_bit_adder_4 (
    .CarryIn(n1_bit_adder_5_carryout), .a(A[20]), .b(xor_5_out), .Sum(result[20]),
    .CarryOut(n1_bit_adder_4_carryout));
  xor xor_4 (xor_4_out, sub, B[21]);
  _1_bit_adder u_1_bit_adder_5 (
    .CarryIn(n1_bit_adder_6_carryout), .a(A[19]), .b(xor_6_out), .Sum(result[19]),
    .CarryOut(n1_bit_adder_5_carryout));
  xor xor_5 (xor_5_out, sub, B[20]);
  xor xor_6 (xor_6_out, sub, B[19]);
  _1_bit_adder u_1_bit_adder_6 (
    .CarryIn(n1_bit_adder_7_carryout), .a(A[18]), .b(xor_7_out), .Sum(result[18]),
    .CarryOut(n1_bit_adder_6_carryout));
  xor xor_7 (xor_7_out, sub, B[18]);
  _1_bit_adder u_1_bit_adder_7 (
    .CarryIn(n1_bit_adder_8_carryout), .a(A[17]), .b(xor_8_out), .Sum(result[17]),
    .CarryOut(n1_bit_adder_7_carryout));
  _1_bit_adder u_1_bit_adder_8 (
    .CarryIn(n1_bit_adder_9_carryout), .a(A[16]), .b(xor_9_out), .Sum(result[16]),
    .CarryOut(n1_bit_adder_8_carryout));
  xor xor_8 (xor_8_out, sub, B[17]);
  _1_bit_adder u_1_bit_adder_9 (
    .CarryIn(n1_bit_adder_10_carryout), .a(A[15]), .b(xor_10_out), .Sum(result[15]),
    .CarryOut(n1_bit_adder_9_carryout));
  xor xor_9 (xor_9_out, sub, B[16]);
  xor xor_10 (xor_10_out, sub, B[15]);
  _1_bit_adder u_1_bit_adder_10 (
    .CarryIn(n1_bit_adder_11_carryout), .a(A[14]), .b(xor_11_out), .Sum(result[14]),
    .CarryOut(n1_bit_adder_10_carryout));
  xor xor_11 (xor_11_out, sub, B[14]);
  _1_bit_adder u_1_bit_adder_11 (
    .CarryIn(n1_bit_adder_12_carryout), .a(A[13]), .b(xor_12_out), .Sum(result[13]),
    .CarryOut(n1_bit_adder_11_carryout));
  _1_bit_adder u_1_bit_adder_12 (
    .CarryIn(n1_bit_adder_13_carryout), .a(A[12]), .b(xor_14_out), .Sum(result[12]),
    .CarryOut(n1_bit_adder_12_carryout));
  xor xor_12 (xor_12_out, sub, B[13]);
  _1_bit_adder u_1_bit_adder_13 (
    .CarryIn(n1_bit_adder_14_carryout), .a(A[11]), .b(xor_13_out), .Sum(result[11]),
    .CarryOut(n1_bit_adder_13_carryout));
  xor xor_13 (xor_13_out, sub, B[11]);
  xor xor_14 (xor_14_out, sub, B[12]);
  _1_bit_adder u_1_bit_adder_14 (
    .CarryIn(n1_bit_adder_15_carryout), .a(A[10]), .b(xor_15_out), .Sum(result[10]),
    .CarryOut(n1_bit_adder_14_carryout));
  xor xor_15 (xor_15_out, sub, B[10]);
  _1_bit_adder u_1_bit_adder_15 (
    .CarryIn(n1_bit_adder_16_carryout), .a(A[9]), .b(xor_16_out), .Sum(result[9]),
    .CarryOut(n1_bit_adder_15_carryout));
  _1_bit_adder u_1_bit_adder_16 (
    .CarryIn(n1_bit_adder_17_carryout), .a(A[8]), .b(xor_17_out), .Sum(result[8]),
    .CarryOut(n1_bit_adder_16_carryout));
  xor xor_16 (xor_16_out, sub, B[9]);
  _1_bit_adder u_1_bit_adder_17 (
    .CarryIn(n1_bit_adder_18_carryout), .a(A[7]), .b(xor_18_out), .Sum(result[7]),
    .CarryOut(n1_bit_adder_17_carryout));
  xor xor_17 (xor_17_out, sub, B[8]);
  xor xor_18 (xor_18_out, sub, B[7]);
  _1_bit_adder u_1_bit_adder_18 (
    .CarryIn(n1_bit_adder_20_carryout), .a(A[6]), .b(xor_19_out), .Sum(result[6]),
    .CarryOut(n1_bit_adder_18_carryout));
  xor xor_19 (xor_19_out, sub, B[6]);
  _1_bit_adder u_1_bit_adder_19 (
    .CarryIn(n1_bit_adder_21_carryout), .a(A[4]), .b(xor_21_out), .Sum(result[4]),
    .CarryOut(n1_bit_adder_19_carryout));
  _1_bit_adder u_1_bit_adder_20 (
    .CarryIn(n1_bit_adder_19_carryout), .a(A[5]), .b(xor_20_out), .Sum(result[5]),
    .CarryOut(n1_bit_adder_20_carryout));
  xor xor_20 (xor_20_out, sub, B[5]);
  _1_bit_adder u_1_bit_adder_21 (
    .CarryIn(n1_bit_adder_22_carryout), .a(A[3]), .b(xor_22_out), .Sum(result[3]),
    .CarryOut(n1_bit_adder_21_carryout));
  xor xor_21 (xor_21_out, sub, B[4]);
  xor xor_22 (xor_22_out, sub, B[3]);
  _1_bit_adder u_1_bit_adder_22 (
    .CarryIn(n1_bit_adder_24_carryout), .a(A[2]), .b(xor_23_out), .Sum(result[2]),
    .CarryOut(n1_bit_adder_22_carryout));
  xor xor_23 (xor_23_out, sub, B[2]);
  _1_bit_adder u_1_bit_adder_23 (
    .CarryIn(sub), .a(A[0]), .b(xor_25_out), .Sum(result[0]), .CarryOut(n1_bit_adder_23_carryout));
  _1_bit_adder u_1_bit_adder_24 (
    .CarryIn(n1_bit_adder_23_carryout), .a(A[1]), .b(xor_24_out), .Sum(result[1]),
    .CarryOut(n1_bit_adder_24_carryout));
  xor xor_24 (xor_24_out, sub, B[1]);
  xor xor_25 (xor_25_out, sub, B[0]);

  // Other names for the same wires on the sheet: _0 = B[0]; _1 = B[1]; _2 = B[2]; _3 = B[3]; _4 = B[4]; _5 = B[5];
  //   _6 = B[6]; _7 = B[7]; _8 = B[8]; _9 = B[9]; _10 = B[10]; _11 = B[11]; _12 = B[12]; _13 = B[13]; _14 = B[14];
  //   _15 = B[15]; _16 = B[16]; _17 = B[17]; _18 = B[18]; _19 = B[19]; _20 = B[20]; _21 = B[21]; _22 = B[22];
  //   _23 = B[23]
endmodule

module _1_bit_adder (
  input  CarryIn,
  input  a,
  input  b,
  output Sum,
  output CarryOut
);

  wire and_1_out, and_2_out, xor_1_out;

  and and_1 (and_1_out, b, a);
  xor xor_1 (xor_1_out, a, b);
  or or_1 (CarryOut, and_1_out, and_2_out);
  and and_2 (and_2_out, xor_1_out, CarryIn);
  xor xor_2 (Sum, CarryIn, xor_1_out);
endmodule
